// Logisim project Raptor32.circ as structural Verilog: 13 circuits, main circuit main
module main (
);

  wire chipset_1_cpuirq, CLK, cpu_1_c, cpu_1_e, cpu_1_i, cpu_1_n, cpu_1_o, cpu_1_z, InstrRE, MemRE, MemWE;
  wire [31:0] cpu_1_ib, cpu_1_x0, cpu_1_x1, cpu_1_x2, cpu_1_x3, cpu_1_x4, cpu_1_x5, cpu_1_x6, cpu_1_x7,
       cpu_1_x8, cpu_1_x9, cpu_1_x10, cpu_1_x11, cpu_1_x12, cpu_1_x13, cpu_1_x14, cpu_1_x15, cpu_1_x16,
       cpu_1_x17, cpu_1_x18, cpu_1_x19, cpu_1_x20, cpu_1_x21, cpu_1_x22, cpu_1_x23, cpu_1_x24, cpu_1_x25,
       cpu_1_x26, cpu_1_x27, cpu_1_x28, cpu_1_x29, cpu_1_x30, cpu_1_x31, InstrAddr, InstrDat, MemAddr,
       MemDat, PC;

  Clock clock_1 (.out(CLK));
  // Probe on InstrAddr
  // Probe on InstrDat
  // Probe on MemAddr
  // Probe on MemDat
  LED Z (.in(cpu_1_z));
  LED N (.in(cpu_1_n));
  LED O (.in(cpu_1_o));
  LED C (.in(cpu_1_c));
  LED I (.in(cpu_1_i));
  LED E (.in(cpu_1_e));
  // Probe on cpu_1_x15
  // Probe on cpu_1_x14
  // Probe on cpu_1_x13
  // Probe on cpu_1_x12
  // Probe on cpu_1_x11
  // Probe on cpu_1_x10
  // Probe on cpu_1_x9
  // Probe on cpu_1_x8
  // Probe on cpu_1_x7
  // Probe on cpu_1_x6
  // Probe on cpu_1_x5
  // Probe on cpu_1_x4
  // Probe on cpu_1_x3
  // Probe on cpu_1_x2
  // Probe on cpu_1_x1
  // Probe on cpu_1_x0
  // Probe on cpu_1_ib
  // Probe on PC
  CPU cpu_1 (
    .InstrMem(InstrDat), .DataMemIn(MemDat), .CLK(CLK), .IRQ(chipset_1_cpuirq), .x9(cpu_1_x9),
    .x10(cpu_1_x10), .x11(cpu_1_x11), .x12(cpu_1_x12), .x13(cpu_1_x13), .x14(cpu_1_x14), .x15(cpu_1_x15),
    .x16(cpu_1_x16), .PC(PC), .x17(cpu_1_x17), .x18(cpu_1_x18), .x19(cpu_1_x19), .x20(cpu_1_x20),
    .x21(cpu_1_x21), .x22(cpu_1_x22), .x23(cpu_1_x23), .x24(cpu_1_x24), .x25(cpu_1_x25), .x26(cpu_1_x26),
    .x0(cpu_1_x0), .x27(cpu_1_x27), .x28(cpu_1_x28), .x29(cpu_1_x29), .x30(cpu_1_x30), .x31(cpu_1_x31),
    .ReadInstrMem(InstrRE), .InstrAddr(InstrAddr), .WriteDataMem(MemWE), .ReadDataMem(MemRE),
    .CPUDataAddr(MemAddr), .DataMemOut(MemDat), .x1(cpu_1_x1), .x2(cpu_1_x2), .x3(cpu_1_x3), .Z(cpu_1_z),
    .N(cpu_1_n), .O(cpu_1_o), .C(cpu_1_c), .I(cpu_1_i), .E(cpu_1_e), .x4(cpu_1_x4), .x5(cpu_1_x5),
    .x6(cpu_1_x6), .IB(cpu_1_ib), .x7(cpu_1_x7), .x8(cpu_1_x8));
  RAM #(.addrWidth(24), .dataWidth(32)) Instr (
    .addr(InstrAddr[23:0]), .oe(InstrRE), .clk(CLK), .din(InstrDat));  // open: we, dout
  // Probe on cpu_1_x16
  // Probe on cpu_1_x17
  // Probe on cpu_1_x18
  // Probe on cpu_1_x19
  // Probe on cpu_1_x20
  // Probe on cpu_1_x21
  // Probe on cpu_1_x22
  // Probe on cpu_1_x23
  // Probe on cpu_1_x24
  // Probe on cpu_1_x25
  // Probe on cpu_1_x26
  // Probe on cpu_1_x27
  // Probe on cpu_1_x28
  // Probe on cpu_1_x29
  // Probe on cpu_1_x30
  // Probe on cpu_1_x31
  Chipset chipset_1 (
    .CPUDataAddr(MemAddr), .CPUDataMemOut(MemDat), .WriteDataMem(MemWE), .ReadDataMem(MemRE),
    .CPUIRQ(chipset_1_cpuirq), .ReadInstrMem(InstrRE), .InstrAddr(InstrAddr), .InstrMem(InstrDat),
    .CPUDataMemIn(MemDat));
  RAM #(.addrWidth(24), .dataWidth(32)) Mem (
    .addr(MemAddr[23:0]), .we(MemWE), .oe(MemRE), .clk(CLK), .din(MemDat));  // open: dout
endmodule

module CPU (
  input  [31:0] InstrMem,
  input  CLK,
  input  IRQ,
  input  [31:0] DataMemIn,
  output [31:0] IB,
  output [31:0] PC,
  output [31:0] x0,
  output [31:0] x1,
  output [31:0] x2,
  output [31:0] x3,
  output [31:0] x4,
  output [31:0] x5,
  output [31:0] x6,
  output [31:0] x7,
  output [31:0] x8,
  output [31:0] x9,
  output [31:0] x10,
  output [31:0] x11,
  output [31:0] x12,
  output [31:0] x13,
  output [31:0] x14,
  output [31:0] x15,
  output [31:0] x16,
  output [31:0] x17,
  output [31:0] x18,
  output [31:0] x19,
  output [31:0] x20,
  output [31:0] x21,
  output [31:0] x22,
  output [31:0] x23,
  output [31:0] x24,
  output [31:0] x25,
  output [31:0] x26,
  output [31:0] x27,
  output [31:0] x28,
  output [31:0] x29,
  output [31:0] x30,
  output [31:0] x31,
  output ReadInstrMem,
  output [31:0] InstrAddr,
  output Z,
  output N,
  output O,
  output C,
  output I,
  output E,
  output WriteDataMem,
  output ReadDataMem,
  output [31:0] CPUDataAddr,
  output [31:0] DataMemOut
);

  wire WE3;
  wire [4:0] A1, A2, A3;
  wire [31:0] RD1, RD2, WD3;

  FetchToDecode FTD (.CLK(CLK));
  RegFile regfile_1 (
    .A1(A1), .A2(A2), .A3(A3), .WD3(WD3), .WE3(WE3), .x10(x10), .x11(x11), .x12(x12), .x13(x13), .x0(x0),
    .x14(x14), .x15(x15), .x16(x16), .x17(x17), .x18(x18), .x19(x19), .x20(x20), .x21(x21), .x22(x22),
    .x23(x23), .x1(x1), .x24(x24), .x25(x25), .x26(x26), .x27(x27), .x28(x28), .x29(x29), .x30(x30),
    .x31(x31), .RD1(RD1), .RD2(RD2), .x2(x2), .x3(x3), .x4(x4), .x5(x5), .x6(x6), .x7(x7), .x8(x8), .x9(x9));
  DecodeToExecute DTE (.CLK(CLK));

  // Other names for the same wires on the sheet: DataAddr[31:0] = CPUDataAddr

  // Notes on the sheet:
  //   Flags go here
  //   Interrupts go here
  //   FETCH
  //   DECODE
  //   EXECUTE
  //   MEMORY
  //   WRIETBACK
  //   Instr and Data Mem separate
  //   Data/Addr goes here
endmodule

module Chipset (
  input  [31:0] CPUDataAddr,
  input  [31:0] CPUDataMemOut,
  output ReadInstrMem,
  output [31:0] InstrAddr,
  output [31:0] InstrMem,
  output WriteDataMem,
  output ReadDataMem,
  output [31:0] CPUDataMemIn,
  output CPUIRQ
);


  // Other names for the same wires on the sheet: DataAddr[31:0] = CPUDataAddr; DataMemIn[31:0] = CPUDataMemIn;
  //   DataMemOut[31:0] = CPUDataMemOut

  // Notes on the sheet:
  //   Chipset
  //   Other inputs TBD once we figure out IO
endmodule

module ALU (
  input  [31:0] src1,
  input  [31:0] src2,
  input  [2:0] ALUOP,
  output [31:0] out1
);


  // Notes on the sheet:
  //   Flags go here
endmodule

module Decode (
  input  [31:0] Instruction
);


  // Other names for the same wires on the sheet: Instr[31:0] = Instruction

  // Notes on the sheet:
  //   Figure out all outputs
endmodule

module RegFile (
  input  [4:0] A1,
  input  [4:0] A2,
  input  [4:0] A3,
  input  [31:0] WD3,
  input  WE3,
  output [31:0] x0,
  output [31:0] x1,
  output [31:0] x2,
  output [31:0] x3,
  output [31:0] x4,
  output [31:0] x5,
  output [31:0] x6,
  output [31:0] x7,
  output [31:0] x8,
  output [31:0] x9,
  output [31:0] x10,
  output [31:0] x11,
  output [31:0] x12,
  output [31:0] x13,
  output [31:0] x14,
  output [31:0] x15,
  output [31:0] x16,
  output [31:0] x17,
  output [31:0] x18,
  output [31:0] x19,
  output [31:0] x20,
  output [31:0] x21,
  output [31:0] x22,
  output [31:0] x23,
  output [31:0] x24,
  output [31:0] x25,
  output [31:0] x26,
  output [31:0] x27,
  output [31:0] x28,
  output [31:0] x29,
  output [31:0] x30,
  output [31:0] x31,
  output [31:0] RD1,
  output [31:0] RD2
);


  // Notes on the sheet:
  //   Write Data
  //   From A1
  //   From A2
endmodule

module SignExtend (
  input  [31:0] Instruction,
  input  [31:0] in_2,
  input  [2:0] InstrType
);


  // Other names for the same wires on the sheet: Instr[31:0] = Instruction; SignExtend[31:0] = in_2

  // Notes on the sheet:
  //   Sign Extend unit
  //   R/I/S/B/U/J Type instr (same order, in binary)
endmodule

module HazardUnit (
);


  // Notes on the sheet:
  //   Hazard Control Unit
endmodule

module Flags (
);


  // Notes on the sheet:
  //   Flags File
endmodule

module FetchToDecode (
  input  CLK
);


  // Notes on the sheet:
  //   Holds Data between the Fetch and Decode Stages
endmodule

module DecodeToExecute (
  input  CLK
);


  // Notes on the sheet:
  //   Holds Data between Decode and Execute Stages
endmodule

module ExecuteToMemory (
  input  CLK
);


  // Notes on the sheet:
  //   Holds Data between Execute and Memory Stages
endmodule

module MemoryToWriteback (
  input  CLK
);


  // Notes on the sheet:
  //   Holds Data between Memory and Writeback Stages
endmodule
